# Fritzing sketch OTOPARK (saved by Fritzing 0.9.4)

parts:
  Parça1 = Arduino Mega 2560 (Rev3)
  U6 = LM2596 step down module
  S1 = Toggle Switch spst [package=THT]
  JACK1 = 2.1mm Barrel Jack with Terminal Block
  J1 = Basic Servo
  J2 = Basic Servo
  M1 = fc-51 [package=THT]
  M2 = fc-51 [package=THT]
  M3 = fc-51 [package=THT]
  M4 = fc-51 [package=THT]
  M5 = fc-51 [package=THT]
  M6 = fc-51 [package=THT]
  M7 = fc-51 [package=THT]
  M8 = fc-51 [package=THT]
  e-radionica_com1 = LM393 LDR breakout [part_number=100027]
  S2 = KY-026
  Mod1 = KY-022 Infrared Receiver Module [package="Breakout board"]
  buz1 = Piezo Buzzer
  LED1 = smd LED [color="White (4500K)" package="1206 [SMD]"]
  LED2 = smd LED [color="White (4500K)" package="1206 [SMD]"]
  LED3 = smd LED [color="White (4500K)" package="1206 [SMD]"]
  LED4 = smd LED [color="White (4500K)" package="1206 [SMD]"]
  R2 = Resistor [tolerance=±5% resistance=330 package="0402 [SMD]"]
  R3 = Resistor [tolerance=±5% resistance=330 package="0402 [SMD]"]
  R4 = Resistor [tolerance=±5% resistance=330 package="0402 [SMD]"]
  R5 = Resistor [tolerance=±5% resistance=330 package="0402 [SMD]"]
  Parça2 = LCD1602-I2C

nets:
  N1: Parça1.SCL, Parça2.SCL
  N2: Parça1.SDA, Parça2.SDA
  N3: Parça1.D11_PWM, M2.pin1
  N4: Parça1.D10_PWM, M1.pin1
  N5: Parça1.D8_PWM, J2.pulse
  GND: Parça1.GND, U6.IN-, U6.OUT-, JACK1.NEG, J2.gnd
  N6: Parça1.VIN, U6.IN+, S1.L1
  N7: Parça1.D3_PWM, Mod1.S
  N8: Parça1.D7_PWM, J1.pulse
  5V: Parça1.5V, Mod1.Vin
  N9: Parça1.D24, S2.pin4
  N10: Parça1.D26, buz1.pin_1
  N11: Parça1.D30, e-radionica_com1.DO
  N12: Parça1.D32, R5.Pin_0
  N13: Parça1.D38, M6.pin1
  N14: Parça1.D40, M7.pin1
  N15: Parça1.D42, M8.pin1
  N16: Parça1.D46, M3.pin1
  N17: Parça1.D48, M5.pin1
  N18: Parça1.D50, M4.pin1
  N19: U6.OUT+, M2.pin3
  N20: S1.COM, JACK1.POS
  N21: LED1.anode, R5.Pin_1
  N22: LED2.anode, R4.Pin_1
  N23: LED3.anode, R2.Pin_1
  N24: LED4.anode, R3.Pin_1

notes:
  9Volt
  9v ---> 5v

custom parts:
  LM2596 step down module: LM2596 DC-DC step down power supply module 3 A.
  Toggle Switch spst: Toggle Switch single pole single throw
  KY-026: ky-026 flame sensor module
  KY-022 Infrared Receiver Module: KY-022 IR receiver module, reacts to 38kHz infrared light.
  Piezo Buzzer: Part from https://www.nutsvolts.com/magazine/article/november2012_SmileysWorkshop modified to be .3 in spacing to match the adafruit buzzer 5V breadboard friendly part.
  LCD1602-I2C: A standard character display, usually with 2x16 characters. Comes in many colors with LCM1602 IIC attached.
